# Fritzing sketch arduino_ir_receiver (saved by Fritzing 0.8.3b)
breadboards: 1

parts:
  TSOP382 = TSOP312.., 314.. [part_number=TSOP382 package=THT]
  1μF = Electrolytic Capacitor [capacitance=1μF package="0405 [SMD, electrolytic]"]
  IR_LED = LED - 5mm [color="Red (633nm)" package="5 mm [THT]"]
  PWR_LED = LED - 5mm [color="Green (555nm)" package="5 mm [THT]"]
  MCP4131 = IC, DIP package, 8 pins [chip_label=MCP4131 part_number="Microchip MCP4131"]
  CdS = PHOTOCELL [package=photocell]
  10kΩ = Resistor [tolerance=±5% resistance=10k package=THT]
  220Ω = Resistor [tolerance=±5% resistance=220 package=THT]
  220Ω_2 = Resistor [tolerance=±5% resistance=220 package=THT]
  MCP4131_2 = IC, DIP package, 8 pins [chip_label=MCP4131 part_number="Microchip MCP4131"]
  Arduino_Micro = Arduino Micro (Rev3)
  47Ω = Resistor [tolerance=±5% resistance=47 package=THT]

nets:
  GND: TSOP382.GND, 1μF.-, MCP4131.pin4, MCP4131.pin7, 10kΩ.Pin_0, 220Ω.Pin_0, 220Ω_2.Pin_0, MCP4131_2.pin4, MCP4131_2.pin7, Arduino_Micro.GND
  5V: TSOP382.Vs, 1μF.+, MCP4131.pin5, MCP4131.pin8, CdS.P$2, MCP4131_2.pin8, Arduino_Micro.5V, 47Ω.Pin_0, 47Ω.Pin_1
  N1: TSOP382.Data, Arduino_Micro.D9_PWM/A9
  N2: IR_LED.cathode, 220Ω_2.Pin_1
  N3: IR_LED.anode, MCP4131_2.pin6
  N4: PWR_LED.cathode, 220Ω.Pin_1
  N5: PWR_LED.anode, MCP4131.pin6
  N6: MCP4131.pin1, Arduino_Micro.D10_PWM/A10
  N7: MCP4131.pin2, MCP4131_2.pin2, Arduino_Micro.SCK
  N8: MCP4131.pin3, MCP4131_2.pin3, Arduino_Micro.MOSI
  N9: CdS.P$1, 10kΩ.Pin_1, Arduino_Micro.A0
  N10: MCP4131_2.pin1, Arduino_Micro.D11_PWM
  N11: MCP4131_2.pin5, Arduino_Micro.D12_PWM/A11
